// Logisim project full_adder.circ as structural Verilog: 1 circuit, main circuit main
module main (
  input  A,
  input  B,
  input  CarryIn,
  output Result,
  output CarryOut
);

  wire and_1_out, and_2_out, xor_1_out;

  xor xor_1 (xor_1_out, A, B);
  and and_1 (and_1_out, xor_1_out, CarryIn);
  and and_2 (and_2_out, B, A);
  xor xor_2 (Result, xor_1_out, CarryIn);
  or or_1 (CarryOut, and_1_out, and_2_out);
endmodule
